# Fritzing sketch AuDo (saved by Fritzing 0.9.9b)

parts:
  Mod2 = ESP32 - CAM
  Part1 = Arduino Uno (Rev3) - ICSP
  M1 = Dagu DGServo 9g (Top view) [part_number=RS001B]
  M2 = Dagu DGServo 9g (Top view) [part_number=RS001B]
  M3 = fc-51 [package=THT]
  Part2 = RFID-RC522-v2
  Part3 = LCD1602-I2C

nets (from the schematic view):
  VCC: Mod2.5V, Part1.5V, M1.vcc, M2.vcc, M3.pin3, Part3.VCC
  GND: Mod2.GND, Part1.GND, M1.gnd, M2.gnd, M3.pin2, Part2.RST, Part3.GND
  N1: Part1.A4/SDA, Part3.SDA
  N2: Part1.A5/SCL, Part3.SCL
  N3: Part1.D2, M3.pin1
  N4: Part1.D5_PWM, M2.pulse
  N5: Part1.D6_PWM, M1.pulse
  N6: Part1.3V3, Part2.3_3V

custom parts:
  ESP32 - CAM: The ESP32-CAM has a very competitive small-size camera module that can operate independently as a minimum system with a footprint of only 27*40.5*4.5mm and a deep sleep current of up to 6mA.
  RFID-RC522-v2: A simple China made RFID-RC522 Reader; do check the pin labels, as this is a MFRC522 based clone.
  LCD1602-I2C: A standard character display, usually with 2x16 characters. Comes in many colors with LCM1602 IIC attached.
